// Digital circuit Processador acho.dig as structural Verilog
module Processador_acho (
);

  wire ctrl_ula_1_p3, ctrl_ula_1_p4, ctrl_ula_1_p5, ctrl_ula_1_p6, MUX_PC, REG_WRITE, Rol_ctrl, uc_1_p5;
  wire [1:0] MUX_ULA, REG_MUX_q;
  wire [3:0] Oper;
  wire [11:0] IR_q;
  wire [15:0] \Memória_d , multiplexer_1_out, multiplexer_2_out, multiplexer_3_out, multiplexer_4_out, PC_q,
       reginaldos_1_p4, reginaldos_1_p5, rol_1_p3, uc_1_p2, ula_1_p7, ULA_A_q, ULA_B_q, ULA_out_q;
  wire [15:3] reginaldos_1_p1, reginaldos_1_p2, undriven;

  Register #(.Bits(16)) PC (.Q(PC_q));  // open: D, C, en
  Multiplexer #(.Bits(16)) multiplexer_1 (.sel(MUX_PC), .in_0(PC_q), .out(multiplexer_1_out));  // open: in_1
  RAMDualPort #(.AddrBits(16), .Bits(16)) \Memória  (.A(multiplexer_1_out), .D(\Memória_d ));  // open: Din, str, C, ld
  Register #(.Bits(16)) IR (.D(\Memória_d ), .Q({Oper, IR_q}));  // open: C, en
  Multiplexer #(.Selector_Bits(2), .Bits(16)) multiplexer_2 (
    .sel(REG_MUX_q), .in_0({reginaldos_1_p1, IR_q[11:9]}), .in_1({reginaldos_1_p2, IR_q[8:6]}),
    .in_2({undriven, IR_q[5:3]}), .out(multiplexer_2_out));  // open: in_3
  // Reginaldos reginaldos_1: pin names not known; wires that end beside it: {reginaldos_1_p1, IR_q[11:9]}, {reginaldos_1_p2, IR_q[8:6]}, multiplexer_2_out, reginaldos_1_p4, reginaldos_1_p5
  Register REG_MUX (.en(REG_WRITE), .Q(REG_MUX_q[0]));  // open: D, C
  // UC uc_1: pin names not known; wires that end beside it: Oper, uc_1_p2, REG_WRITE, MUX_PC, uc_1_p5, MUX_ULA, Rol_ctrl
  BitExtender Ext_Sinal (.in({Oper, IR_q[11:8]}), .out(uc_1_p2));
  Register #(.Bits(16)) ULA_B (.D(reginaldos_1_p5), .Q(ULA_B_q));  // open: C, en
  Register #(.Bits(16)) ULA_A (.D(reginaldos_1_p4), .Q(ULA_A_q));  // open: C, en
  // Ctrl_ULA ctrl_ula_1: pin names not known; wires that end beside it: uc_1_p2, IR_q[2:0], ctrl_ula_1_p3, ctrl_ula_1_p4, ctrl_ula_1_p5, ctrl_ula_1_p6
  Multiplexer #(.Selector_Bits(2), .Bits(16)) multiplexer_3 (
    .in_1(ULA_B_q), .in_2(16'h1), .in_3(uc_1_p2), .out(multiplexer_3_out));  // open: sel, in_0
  Multiplexer #(.Bits(16)) multiplexer_4 (.sel(uc_1_p5), .in_0(PC_q), .in_1(ULA_A_q), .out(multiplexer_4_out));
  // ULA ula_1: pin names not known; wires that end beside it: multiplexer_4_out, multiplexer_3_out, ctrl_ula_1_p3, ctrl_ula_1_p4, ctrl_ula_1_p5, ctrl_ula_1_p6, ula_1_p7
  Register #(.Bits(16)) ULA_out (.D(ula_1_p7), .Q(ULA_out_q));  // open: C, en
  // Rol rol_1: pin names not known; wires that end beside it: Rol_ctrl, multiplexer_4_out, rol_1_p3
  Multiplexer #(.Selector_Bits(2), .Bits(16)) multiplexer_5 (
    .sel(MUX_ULA), .in_0(ULA_out_q), .in_1(rol_1_p3));  // open: in_2, in_3, out
  // Pins of 3 and 16 bits meet at {undriven, IR_q[5:3]}
  // Pins of 3 and 16 bits meet at {reginaldos_1_p2, IR_q[8:6]}
  // Pins of 3 and 16 bits meet at {reginaldos_1_p1, IR_q[11:9]}
  // Pins of 1 and 2 bits meet at REG_MUX_q
endmodule
