// Digital circuit ULA.dig as structural Verilog
module ULA (
  input  [1:0] OP,
  input  [15:0] A,
  input  [15:0] B,
  input  Ainv,
  input  Binv,
  input  Cin,
  output [15:0] \Saída_geral ,
  output Cout,
  output Zero,
  output Overflow
);

  wire xnor_1_out;
  wire [0:0] comparator_1_lt;
  wire [15:0] add_1_s, and_1_out, multiplexer_1_out, multiplexer_2_out, multiplexer_3_out, not_1_out,
       not_2_out, or_1_out, xor_1_out;

  assign not_1_out = ~A;  // Not not_1, 16 bits wide
  Multiplexer #(.Bits(16)) multiplexer_1 (.sel(Binv), .in_0(B), .in_1(not_2_out), .out(multiplexer_1_out));
  assign not_2_out = ~B;  // Not not_2, 16 bits wide
  Multiplexer #(.Bits(16)) multiplexer_2 (.sel(Ainv), .in_0(A), .in_1(not_1_out), .out(multiplexer_2_out));
  assign and_1_out = multiplexer_2_out & multiplexer_1_out;  // And and_1, 16 bits wide
  assign or_1_out = multiplexer_2_out | multiplexer_1_out;  // Or or_1, 16 bits wide
  Add #(.Bits(16)) add_1 (.a(multiplexer_2_out), .b(multiplexer_1_out), .c_i(Cin), .s(add_1_s), .c_o(Cout));
  Comparator #(.Bits(16)) comparator_1 (
    .a(multiplexer_2_out), .b(multiplexer_1_out), .lt(comparator_1_lt[0]));  // open: gt, eq
  assign xor_1_out = multiplexer_2_out ^ multiplexer_1_out;  // XOr xor_1, 16 bits wide
  xnor xnor_1 (xnor_1_out, multiplexer_2_out[15], multiplexer_1_out[15]);
  Multiplexer #(.Bits(16)) multiplexer_3 (
    .sel(Cin), .in_0({{15{1'b0}}, comparator_1_lt[0]}), .in_1(xor_1_out), .out(multiplexer_3_out));
  xor xor_2 (Overflow, add_1_s[15], xnor_1_out);
  nor nor_1 (Zero, add_1_s[0], add_1_s[1], add_1_s[2], add_1_s[3], add_1_s[4], add_1_s[5], add_1_s[6], add_1_s[7], add_1_s[8], add_1_s[9], add_1_s[10], add_1_s[11], add_1_s[12], add_1_s[13], add_1_s[14], add_1_s[15]);
  Multiplexer #(.Selector_Bits(2), .Bits(16)) multiplexer_4 (
    .sel(OP), .in_0(and_1_out), .in_1(or_1_out), .in_2(add_1_s), .in_3(multiplexer_3_out), .out(\Saída_geral ));

  // Notes on the sheet:
  //   OP: Funciona como seletor de saída.
  //   Binv: Bit menos significativo da Func.
  //   e
endmodule
